// Logisim project clock.circ as structural Verilog: 5 circuits, main circuit main
module main (
);

  wire a0, a1, a2, a3, AM_PM, and_1_out, and_3_out, b0, b1, b2, b3, c0, c1, c2, c3, CLK_1Hz, d0, d1, d2, d3,
       d_ff_1_q, d_ff_1_qn, d_ff_3_qn, d_ff_4_qn, e0, e1, e2, e3, f0, f1, f2, f3, g0, g1, g2, g3,
       hour_counter_1_hour_ones_0, hour_counter_1_hour_ones_1, hour_counter_1_hour_ones_2,
       hour_counter_1_hour_ones_3, hour_counter_1_hour_rollover, hour_counter_1_hour_tens_0,
       hour_counter_1_hour_tens_1, hour_counter_1_hour_tens_2, hour_counter_1_hour_tens_3,
       min_counter_1_min_ones_0, min_counter_1_min_ones_1, min_counter_1_min_ones_2,
       min_counter_1_min_ones_3, min_counter_1_min_rollover, min_counter_1_min_tens_0,
       min_counter_1_min_tens_1, min_counter_1_min_tens_2, min_counter_1_min_tens_3, not_1_out, plus_HOUR,
       plus_HOUR_BUTTON, plus_MIN, plus_MIN_BUTTON, RESET, RESET_BUTTON, RESET_STATE,
       sec_counter_1_sec_rollover, transistor_1_out, transistor_2_out;

  Clock clock_1 (.out(CLK_1Hz));
  _7_Segment_Display u_7_segment_display_1 (.g(g0), .f(f0), .a(a0), .b(b0), .e(e0), .d(d0), .c(c0));  // open: dp
  and and_1 (and_1_out, CLK_1Hz, not_1_out);
  not not_1 (not_1_out, RESET_STATE);
  _7_Segment_Display u_7_segment_display_2 (.g(g1), .f(f1), .a(a1), .b(b1), .e(e1), .d(d1), .c(c1));  // open: dp
  and and_2 (plus_HOUR, RESET_STATE, plus_HOUR_BUTTON);
  D_Flip_Flop d_ff_1 (.clk(RESET_BUTTON), .D(d_ff_1_qn), .Q(d_ff_1_q), .Qn(d_ff_1_qn));  // open: preset, en, reset
  and and_3 (and_3_out, d_ff_1_q, d_ff_3_qn);
  _7_Segment_Display u_7_segment_display_3 (.g(g2), .f(f2), .a(a2), .b(b2), .e(e2), .d(d2), .c(c2));  // open: dp
  sec_counter sec_counter_1 (.CLK_1Hz(and_1_out), .sec_rollover(sec_counter_1_sec_rollover), .RESET(RESET));
  D_Flip_Flop d_ff_2 (.clk(CLK_1Hz), .D(and_3_out), .Q(RESET));  // open: Qn, preset, en, reset
  _7_Segment_Display u_7_segment_display_4 (.g(g3), .f(f3), .a(a3), .b(b3), .e(e3), .d(d3), .c(c3));  // open: dp
  and and_4 (plus_MIN, RESET_STATE, plus_MIN_BUTTON);
  LED PM (.in(transistor_2_out));
  D_Flip_Flop d_ff_3 (.clk(CLK_1Hz), .D(d_ff_1_q), .Q(RESET_STATE), .Qn(d_ff_3_qn));  // open: preset, en, reset
  Button SET_TIME (.out(RESET_BUTTON));
  LED led_1 (.in(transistor_1_out));
  Button u_plus_HOUR (.out(plus_HOUR_BUTTON));
  Button u_plus_MIN (.out(plus_MIN_BUTTON));
  min_counter min_counter_1 (
    .sec_rollover(sec_counter_1_sec_rollover), .min_rollover(min_counter_1_min_rollover),
    .min_ones_0(min_counter_1_min_ones_0), .min_ones_1(min_counter_1_min_ones_1),
    .min_ones_2(min_counter_1_min_ones_2), .min_ones_3(min_counter_1_min_ones_3),
    .min_tens_0(min_counter_1_min_tens_0), .min_tens_1(min_counter_1_min_tens_1),
    .min_tens_2(min_counter_1_min_tens_2), .min_tens_3(min_counter_1_min_tens_3), .plus_MIN(plus_MIN),
    .RESET(RESET));
  // _7_segment_display_driver 7_segment_display_driver_1: pin names not known; wires that end beside it: min_counter_1_min_ones_3, min_counter_1_min_ones_2, min_counter_1_min_ones_1, min_counter_1_min_ones_0, a3, b3, c3, d3, e3, f3, g3
  // _7_segment_display_driver 7_segment_display_driver_2: pin names not known; wires that end beside it: min_counter_1_min_tens_3, min_counter_1_min_tens_2, min_counter_1_min_tens_1, min_counter_1_min_tens_0, a2, b2, c2, d2, e2, f2, g2
  Transistor #(.\type ("n"), .gate("br")) transistor_1 (.in(1'b1), .out(transistor_1_out), .gate(RESET_STATE));
  Pull_Resistor pull_resistor_1 (.node(transistor_1_out));
  Transistor #(.\type ("n"), .gate("br")) transistor_2 (.in(1'b1), .out(transistor_2_out), .gate(AM_PM));
  Pull_Resistor pull_resistor_2 (.node(transistor_2_out));
  hour_counter hour_counter_1 (
    .min_rollover(min_counter_1_min_rollover), .hour_rollover(hour_counter_1_hour_rollover),
    .hour_ones_1(hour_counter_1_hour_ones_1), .hour_ones_2(hour_counter_1_hour_ones_2),
    .hour_ones_3(hour_counter_1_hour_ones_3), .hour_tens_0(hour_counter_1_hour_tens_0),
    .hour_tens_1(hour_counter_1_hour_tens_1), .hour_tens_2(hour_counter_1_hour_tens_2),
    .hour_tens_3(hour_counter_1_hour_tens_3), .hour_ones_0(hour_counter_1_hour_ones_0), .RESET(RESET),
    .plus_HOUR(plus_HOUR));
  // _7_segment_display_driver 7_segment_display_driver_3: pin names not known; wires that end beside it: hour_counter_1_hour_ones_3, hour_counter_1_hour_ones_2, hour_counter_1_hour_ones_1, hour_counter_1_hour_ones_0, a1, b1, c1, d1, e1, f1, g1
  // _7_segment_display_driver 7_segment_display_driver_4: pin names not known; wires that end beside it: hour_counter_1_hour_tens_3, hour_counter_1_hour_tens_2, hour_counter_1_hour_tens_1, hour_counter_1_hour_tens_0, a0, b0, c0, d0, e0, f0, g0
  D_Flip_Flop d_ff_4 (
    .clk(hour_counter_1_hour_rollover), .D(d_ff_4_qn), .Q(AM_PM), .Qn(d_ff_4_qn), .reset(RESET));  // open: preset, en

  // Notes on the sheet:
  //   Set tick frequency in Logisim to 2Hz
endmodule

module sec_counter (
  input  CLK_1Hz,
  input  RESET,
  output sec_rollover
);

  wire _59, and_7_out, and_8_out, and_10_out, and_11_out, and_12_out, and_13_out, and_14_out, and_15_out, D0,
       D1, D2, D3, D4, D5, d_ff_2_q, d_ff_2_qn, d_ff_3_q, d_ff_4_q, d_ff_4_qn, d_ff_5_q, d_ff_6_q, d_ff_7_q,
       not_1_out, xor_1_out, xor_2_out, xor_3_out, xor_4_out, xor_5_out;

  D_Flip_Flop d_ff_1 (.clk(CLK_1Hz), .D(_59), .Q(sec_rollover));  // open: Qn, preset, en, reset
  and and_1 (D0, d_ff_2_qn, not_1_out);
  and and_2 (D1, xor_1_out, not_1_out);
  and and_3 (D2, xor_2_out, not_1_out);
  and and_4 (D3, xor_3_out, not_1_out);
  and and_5 (D4, xor_4_out, not_1_out);
  and and_6 (D5, xor_5_out, not_1_out);
  not not_1 (not_1_out, _59);
  xor xor_1 (xor_1_out, d_ff_2_q, d_ff_3_q);
  xor xor_2 (xor_2_out, and_12_out, d_ff_4_q);
  xor xor_3 (xor_3_out, and_10_out, d_ff_5_q);
  xor xor_4 (xor_4_out, and_8_out, d_ff_6_q);
  xor xor_5 (xor_5_out, and_7_out, d_ff_7_q);
  and and_7 (and_7_out, and_8_out, d_ff_6_q);
  and and_8 (and_8_out, and_10_out, d_ff_5_q);
  and and_9 (_59, and_13_out, and_11_out);
  and and_10 (and_10_out, and_12_out, d_ff_4_q);
  and and_11 (and_11_out, and_14_out, and_15_out);
  D_Flip_Flop d_ff_2 (.clk(CLK_1Hz), .D(D0), .Q(d_ff_2_q), .Qn(d_ff_2_qn), .reset(RESET));  // open: preset, en
  and and_12 (and_12_out, d_ff_2_q, d_ff_3_q);
  and and_13 (and_13_out, d_ff_2_q, d_ff_3_q);
  and and_14 (and_14_out, d_ff_4_qn, d_ff_5_q);
  and and_15 (and_15_out, d_ff_6_q, d_ff_7_q);
  D_Flip_Flop d_ff_3 (.clk(CLK_1Hz), .D(D1), .Q(d_ff_3_q), .reset(RESET));  // open: Qn, preset, en
  D_Flip_Flop d_ff_4 (.clk(CLK_1Hz), .D(D2), .Q(d_ff_4_q), .Qn(d_ff_4_qn), .reset(RESET));  // open: preset, en
  D_Flip_Flop d_ff_5 (.clk(CLK_1Hz), .D(D3), .Q(d_ff_5_q), .reset(RESET));  // open: Qn, preset, en
  D_Flip_Flop d_ff_6 (.clk(CLK_1Hz), .D(D4), .Q(d_ff_6_q), .reset(RESET));  // open: Qn, preset, en
  D_Flip_Flop d_ff_7 (.clk(CLK_1Hz), .D(D5), .Q(d_ff_7_q), .reset(RESET));  // open: Qn, preset, en

  // Notes on the sheet:
  //   Inputs
  //   Outputs
endmodule

module min_counter (
  input  sec_rollover,
  input  RESET,
  input  plus_MIN,
  output min_rollover,
  output min_ones_0,
  output min_ones_1,
  output min_ones_2,
  output min_ones_3,
  output min_tens_0,
  output min_tens_1,
  output min_tens_2,
  output min_tens_3
);

  wire _9, _59, and_1_out, and_2_out, and_3_out, and_4_out, and_5_out, and_6_out, and_7_out, and_8_out,
       and_10_out, and_12_out, and_13_out, and_14_out, and_15_out, d_ff_3_qn, d_ff_4_qn, d_ff_5_qn,
       d_ff_6_qn, d_ff_7_qn, d_ff_10_qn, min_ones_rollover, n4_stage_counter_logic_1_d0,
       n4_stage_counter_logic_1_d1, n4_stage_counter_logic_1_d2, n4_stage_counter_logic_1_d3,
       n4_stage_counter_logic_2_d0, n4_stage_counter_logic_2_d1, n4_stage_counter_logic_2_d2,
       n4_stage_counter_logic_2_d3, not_1_out, not_2_out, sec_rollover_t;

  D_Flip_Flop d_ff_1 (.clk(sec_rollover_t), .D(_9), .Q(min_ones_rollover));  // open: Qn, preset, en, reset
  D_Flip_Flop d_ff_2 (.clk(sec_rollover_t), .D(_59), .Q(min_rollover));  // open: Qn, preset, en, reset
  or or_1 (sec_rollover_t, sec_rollover, plus_MIN);
  and and_1 (and_1_out, not_1_out, n4_stage_counter_logic_1_d0);
  and and_2 (and_2_out, not_1_out, n4_stage_counter_logic_1_d1);
  and and_3 (and_3_out, not_1_out, n4_stage_counter_logic_1_d2);
  and and_4 (and_4_out, not_1_out, n4_stage_counter_logic_1_d3);
  not not_1 (not_1_out, _9);
  and and_5 (and_5_out, not_2_out, n4_stage_counter_logic_2_d0);
  and and_6 (and_6_out, not_2_out, n4_stage_counter_logic_2_d1);
  and and_7 (and_7_out, not_2_out, n4_stage_counter_logic_2_d2);
  and and_8 (and_8_out, not_2_out, n4_stage_counter_logic_2_d3);
  not not_2 (not_2_out, _59);
  and and_9 (_59, and_14_out, _9);
  _4_stage_counter_logic u_4_stage_counter_logic_1 (
    .D0(n4_stage_counter_logic_1_d0), .D1(n4_stage_counter_logic_1_d1), .D2(n4_stage_counter_logic_1_d2),
    .D3(n4_stage_counter_logic_1_d3), .nQ0(d_ff_3_qn), .Q0(min_ones_0), .Q1(min_ones_1), .Q2(min_ones_2),
    .Q3(min_ones_3));
  and and_10 (and_10_out, min_ones_0, d_ff_5_qn);
  and and_11 (_9, and_10_out, and_12_out);
  and and_12 (and_12_out, d_ff_7_qn, min_ones_3);
  _4_stage_counter_logic u_4_stage_counter_logic_2 (
    .D0(n4_stage_counter_logic_2_d0), .D1(n4_stage_counter_logic_2_d1), .D2(n4_stage_counter_logic_2_d2),
    .D3(n4_stage_counter_logic_2_d3), .nQ0(d_ff_4_qn), .Q0(min_tens_0), .Q1(min_tens_1), .Q2(min_tens_2),
    .Q3(min_tens_3));
  and and_13 (and_13_out, min_tens_0, d_ff_6_qn);
  and and_14 (and_14_out, and_13_out, and_15_out);
  and and_15 (and_15_out, min_tens_2, d_ff_10_qn);
  D_Flip_Flop d_ff_3 (
    .clk(sec_rollover_t), .D(and_1_out), .Q(min_ones_0), .Qn(d_ff_3_qn), .reset(RESET));  // open: preset, en
  D_Flip_Flop d_ff_4 (
    .clk(min_ones_rollover), .D(and_5_out), .Q(min_tens_0), .Qn(d_ff_4_qn), .reset(RESET));  // open: preset, en
  D_Flip_Flop d_ff_5 (
    .clk(sec_rollover_t), .D(and_2_out), .Q(min_ones_1), .Qn(d_ff_5_qn), .reset(RESET));  // open: preset, en
  D_Flip_Flop d_ff_6 (
    .clk(min_ones_rollover), .D(and_6_out), .Q(min_tens_1), .Qn(d_ff_6_qn), .reset(RESET));  // open: preset, en
  D_Flip_Flop d_ff_7 (
    .clk(sec_rollover_t), .D(and_3_out), .Q(min_ones_2), .Qn(d_ff_7_qn), .reset(RESET));  // open: preset, en
  D_Flip_Flop d_ff_8 (.clk(min_ones_rollover), .D(and_7_out), .Q(min_tens_2), .reset(RESET));  // open: Qn, preset, en
  D_Flip_Flop d_ff_9 (.clk(sec_rollover_t), .D(and_4_out), .Q(min_ones_3), .reset(RESET));  // open: Qn, preset, en
  D_Flip_Flop d_ff_10 (
    .clk(min_ones_rollover), .D(and_8_out), .Q(min_tens_3), .Qn(d_ff_10_qn), .reset(RESET));  // open: preset, en

  // Notes on the sheet:
  //   Inputs
  //   Outputs
endmodule

module hour_counter (
  input  min_rollover,
  input  plus_HOUR,
  input  RESET,
  output hour_rollover,
  output hour_ones_0,
  output hour_ones_1,
  output hour_ones_2,
  output hour_ones_3,
  output hour_tens_0,
  output hour_tens_1,
  output hour_tens_2,
  output hour_tens_3
);

  wire _0, _1, _9, _11, and_1_out, and_2_out, and_3_out, and_4_out, and_5_out, and_6_out, and_7_out,
       and_8_out, and_9_out, and_13_out, and_14_out, and_15_out, and_16_out, and_17_out, and_18_out,
       and_19_out, d_ff_3_qn, d_ff_4_qn, d_ff_5_qn, d_ff_6_qn, d_ff_7_qn, d_ff_8_qn, d_ff_9_qn, d_ff_10_qn,
       hour_ones_1_t, hour_ones_rollover, hour_tens_0_t, min_rollover_t, n4_stage_counter_logic_1_d0,
       n4_stage_counter_logic_1_d1, n4_stage_counter_logic_1_d2, n4_stage_counter_logic_1_d3,
       n4_stage_counter_logic_2_d0, n4_stage_counter_logic_2_d1, n4_stage_counter_logic_2_d2,
       n4_stage_counter_logic_2_d3, not_2_out, not_3_out, not_4_out, or_3_out, or_4_out, or_5_out, or_6_out,
       or_7_out, or_8_out, or_9_out, or_11_out;

  or or_1 (hour_ones_1, hour_ones_1_t, _0);
  or or_2 (hour_tens_0, hour_tens_0_t, _0);
  or or_3 (or_3_out, hour_ones_0, hour_ones_1_t);
  or or_4 (or_4_out, or_3_out, or_5_out);
  or or_5 (or_5_out, hour_ones_2, hour_ones_3);
  or or_6 (or_6_out, hour_tens_0_t, hour_tens_1);
  or or_7 (or_7_out, or_6_out, or_8_out);
  or or_8 (or_8_out, hour_tens_2, hour_tens_3);
  or or_9 (or_9_out, _9, _11);
  or or_10 (min_rollover_t, min_rollover, plus_HOUR);
  or or_11 (or_11_out, or_4_out, or_7_out);
  D_Flip_Flop d_ff_1 (.clk(min_rollover_t), .D(or_9_out), .Q(hour_ones_rollover));  // open: Qn, preset, en, reset
  D_Flip_Flop d_ff_2 (.clk(min_rollover_t), .D(_11), .Q(hour_rollover));  // open: Qn, preset, en, reset
  not not_1 (_0, or_11_out);
  and and_1 (and_1_out, and_5_out, n4_stage_counter_logic_1_d0);
  and and_2 (and_2_out, and_5_out, n4_stage_counter_logic_1_d1);
  and and_3 (and_3_out, and_5_out, n4_stage_counter_logic_1_d2);
  and and_4 (and_4_out, and_5_out, n4_stage_counter_logic_1_d3);
  and and_5 (and_5_out, not_2_out, not_4_out);
  not not_2 (not_2_out, _9);
  and and_6 (and_6_out, not_3_out, n4_stage_counter_logic_2_d0);
  and and_7 (and_7_out, not_3_out, n4_stage_counter_logic_2_d1);
  and and_8 (and_8_out, not_3_out, n4_stage_counter_logic_2_d2);
  and and_9 (and_9_out, not_3_out, n4_stage_counter_logic_2_d3);
  not not_3 (not_3_out, _11);
  and and_10 (_11, and_13_out, _1);
  not not_4 (not_4_out, _11);
  and and_11 (_9, and_14_out, and_15_out);
  and and_12 (_1, and_16_out, and_17_out);
  and and_13 (and_13_out, and_18_out, and_19_out);
  _4_stage_counter_logic u_4_stage_counter_logic_1 (
    .D0(n4_stage_counter_logic_1_d0), .D1(n4_stage_counter_logic_1_d1), .D2(n4_stage_counter_logic_1_d2),
    .D3(n4_stage_counter_logic_1_d3), .nQ0(d_ff_3_qn), .Q0(hour_ones_0), .Q1(hour_ones_1_t),
    .Q2(hour_ones_2), .Q3(hour_ones_3));
  and and_14 (and_14_out, hour_ones_0, d_ff_5_qn);
  and and_15 (and_15_out, d_ff_7_qn, hour_ones_3);
  and and_16 (and_16_out, hour_ones_0, d_ff_5_qn);
  and and_17 (and_17_out, d_ff_7_qn, d_ff_9_qn);
  _4_stage_counter_logic u_4_stage_counter_logic_2 (
    .D0(n4_stage_counter_logic_2_d0), .D1(n4_stage_counter_logic_2_d1), .D2(n4_stage_counter_logic_2_d2),
    .D3(n4_stage_counter_logic_2_d3), .nQ0(d_ff_4_qn), .Q0(hour_tens_0_t), .Q1(hour_tens_1),
    .Q2(hour_tens_2), .Q3(hour_tens_3));
  and and_18 (and_18_out, hour_tens_0_t, d_ff_6_qn);
  and and_19 (and_19_out, d_ff_8_qn, d_ff_10_qn);
  D_Flip_Flop d_ff_3 (
    .clk(min_rollover_t), .D(and_1_out), .Q(hour_ones_0), .Qn(d_ff_3_qn), .reset(RESET));  // open: preset, en
  D_Flip_Flop d_ff_4 (
    .clk(hour_ones_rollover), .D(and_6_out), .Q(hour_tens_0_t), .Qn(d_ff_4_qn), .reset(RESET));  // open: preset, en
  D_Flip_Flop d_ff_5 (
    .clk(min_rollover_t), .D(and_2_out), .Q(hour_ones_1_t), .Qn(d_ff_5_qn), .reset(RESET));  // open: preset, en
  D_Flip_Flop d_ff_6 (
    .clk(hour_ones_rollover), .D(and_7_out), .Q(hour_tens_1), .Qn(d_ff_6_qn), .reset(RESET));  // open: preset, en
  D_Flip_Flop d_ff_7 (
    .clk(min_rollover_t), .D(and_3_out), .Q(hour_ones_2), .Qn(d_ff_7_qn), .reset(RESET));  // open: preset, en
  D_Flip_Flop d_ff_8 (
    .clk(hour_ones_rollover), .D(and_8_out), .Q(hour_tens_2), .Qn(d_ff_8_qn), .reset(RESET));  // open: preset, en
  D_Flip_Flop d_ff_9 (
    .clk(min_rollover_t), .D(and_4_out), .Q(hour_ones_3), .Qn(d_ff_9_qn), .reset(RESET));  // open: preset, en
  D_Flip_Flop d_ff_10 (
    .clk(hour_ones_rollover), .D(and_9_out), .Q(hour_tens_3), .Qn(d_ff_10_qn), .reset(RESET));  // open: preset, en

  // Notes on the sheet:
  //   Inputs
  //   Outputs
  //   If hour = 0, display it as 12
endmodule

module _4_stage_counter_logic (
  input  nQ0,
  input  Q0,
  input  Q1,
  input  Q2,
  input  Q3,
  output D0,
  output D1,
  output D2,
  output D3
);

  wire and_1_out, and_2_out;

  xor xor_1 (D1, Q0, Q1);
  xor xor_2 (D2, and_2_out, Q2);
  xor xor_3 (D3, and_1_out, Q3);
  and and_1 (and_1_out, and_2_out, Q2);
  and and_2 (and_2_out, Q0, Q1);

  assign D0 = nQ0;
endmodule
